# Fritzing sketch atmega88-bootloading (saved by Fritzing 0.7.1b)
breadboards: 1

parts:
  J1 = female pin header, 6 pins [form="♀ (female)"]
  J2 = male pin header, 3 pins [form="♂ (male)"]
  J3 = male pin header, 3 pins [form="♂ (male)"]
  R1 = Resistor [tolerance=±5% resistance=10k package=THT]
  C1 = Tantalum Capacitor [capacitance=0.1µF package="100 mil [THT, tantalum]"]
  LED1 = LED - 5mm [color="Red (633nm)" package="5 mm [THT]"]
  U1 = atmega168 [part_number=ATmega88-20PU package="DIP28 [THT]"]

nets:
  N1: J1.pin1, LED1.cathode, U1.Pin_8, U1.Pin_22
  N2: J1.pin3, J3.pin1, R1.Pin_0, U1.Pin_6, U1.Pin_21
  N3: J1.pin4, U1.Pin_16
  N4: J1.pin5, U1.Pin_17
  N5: J1.pin6, C1.-
  N6: J2.pin1, U1.Pin_4
  N7: J2.pin2, LED1.anode, U1.Pin_5
  N8: J2.pin3, R1.Pin_1, C1.+, U1.Pin_15
  N9: J3.pin2, U1.Pin_3

notes:
  AVR ISP programmer interface
  USB programmer
